# Fritzing sketch Hygrometer-Pump-Sketch (saved by Fritzing 0.9.3b)
breadboards: 1

parts:
  Part1 = Arduino Uno (Rev3)
  Humidity_Sensor = Humidity Sensor - HIH-4030 Breakout  # not connected
  P2N2222A = NPN-Transistor [part_number=P2N2222A package="TO92 [THT]"]
  Parastaltic_Pump = DC Motor  # not connected
  1N4001_1-AMP_Diode = Diode [package=diode-hv]

nets:
  N1: Part1.A1, P2N2222A.C
  N2: Part1.VIN, 1N4001_1-AMP_Diode.C

notes:
  CAUTION: Make sure to orient diode and transistor correctly.
  This is actually a 12V DC Peristaltic dosing pump used to pump the water.

// code stored in the sketch: Hygrometer-Pump-Sketch.ino
// sensor A0 - Hygrometer
int sensorPinA0 = 0;
// sensor A1 - Parastaltic pump
int motorPin = A1;

int pumpTime = 5000;
int waitTime = 10000;

void setup(){
  Serial.begin(9600);
  pinMode(motorPin, OUTPUT);
}

void loop(){
  int sensorValue = analogRead(sensorPinA0);
  Serial.println(sensorValue);
  delay(10);
  if(sensorValue > 900){
    digitalWrite(motorPin, HIGH);
    //delay(pumpTime);
    //delay(waitTime);
  } else {
    digitalWrite(motorPin, LOW);  
  }
}
